# Fritzing sketch all (saved by Fritzing 0.9.10b)

parts:
  M1 = DC Motor [voltage_(max)=6V voltage_(min)=3V]  # not connected
  Part1 = Adafruit DRV8833 DC/Stepper Motor Driver [part_number="Adafruit #3297"]  # not connected
  Зарядник = Lithium battery charger [package="DIP (Dual Inline) [THT]"]
  18650_аккум = 18650 holder [package="DIP (Dual Inline) [THT]"]
  Повышайка = XL6009 [part_number=XL6009 package=TO263]
  M2 = gear-motor
  Драйвер = Adafruit DRV8833 DC/Stepper Motor Driver [part_number="Adafruit #3297"]

nets:
  N1: Зарядник.Battery+, 18650_аккум.holder_+
  N2: Зарядник.Battery-, 18650_аккум.holder_-
  5V: Повышайка.pin_4
  N3: M2.pin_1, Драйвер.AOUT2
  N4: M2.pin_2, Драйвер.AOUT1

notes:
  задняя ось

custom parts:
  Adafruit DRV8833 DC/Stepper Motor Driver: Spin two DC motors or step one bi-polar or uni-polar stepper with up to 1.2A per channel using the DRV8833. This motor driver chip is a nice alternative to the TB6612 driver. Like that chip, you get 2 full H-bridges, but this chip is better for low voltage uses (can run from 2.7V up to 10.8V motor power) and has built in current limiting capability. We set it up for 1A current limiting so you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
  Lithium battery charger: USB зарядник для литиевых аккумуляторов + защита от КЗ и переразряда
  18650 holder: Акум формата 18650 в холдере
